// Logisim project final_alt_task1.circ as structural Verilog: 2 circuits, main circuit DUT
module DUT (
  input  [7:0] X1,
  input  [7:0] Y1,
  input  [7:0] X2,
  input  [7:0] Y2,
  input  REQ,
  input  CLK,
  input  RST,
  output [11:0] DIST,
  output ACK
);


  // Notes on the sheet:
  //   Please put your design below. You may also use subcircuits.
  //   However, do not move, rename, add, or delete any pins.
endmodule

module TB (
  input  [7:0] X1,
  input  [7:0] Y1,
  input  [7:0] X2,
  input  [7:0] Y2,
  input  REQ,
  input  RST,
  output [11:0] DIST,
  output ACK
);

  wire CLK_out, or_1_out, RESET_out;

  Clock sysclk ();  // open: out
  Button RESET (.out(RESET_out));
  Clock #(.highDuration(2), .lowDuration(2)) CLK (.out(CLK_out));
  or or_1 (or_1_out, RESET_out, RST);
  DUT dut_1 (.X1(X1), .Y1(Y1), .X2(X2), .Y2(Y2), .REQ(REQ), .CLK(CLK_out), .RST(or_1_out), .DIST(DIST), .ACK(ACK));

  // Notes on the sheet:
  //   DO NOT MODIFY THIS
  //   YOU MAY TEST YOUR CIRCUITS USING THIS TO MAKE SURE YOU HAVE NOT ALTERED PIN OUT
endmodule
