// Logisim project final_alt_task1_tester.circ as structural Verilog: 2 circuits, main circuit Tester
module Tester (
  output halt,
  output [17:0] CYCLE,
  output RST,
  output REQ,
  output ACK,
  output [7:0] X1,
  output [7:0] Y1,
  output [7:0] X2,
  output [7:0] Y2,
  output [11:0] DIST,
  output [15:0] CNTRST,
  output [15:0] CNTREQ,
  output [15:0] CNTACK,
  output ASSERTIONS
);

  wire and_1_out, and_2_out, CLK_out, counter_1_carry, counter_2_carry, countnegedges16b_1_reachedmax,
       EdgeACK, FEdgeACK, FEdgeREQ, GT2RST, not_1_out, not_2_out, not_3_out, NXTOP, OLDNXTOP, or_4_out,
       pulsecounter16b_2_reachedmax, REdgeACK, REdgeREQ, REdgeRST;
  wire [3:0] counter_2_q;
  wire [15:0] subtractor_1_out;
  wire [31:0] DINb, EdgeCases_data, multiplexer_2_out, random_1_out, random_2_out, register_1_q;

  Clock sysclk ();  // open: out
  Clock CLK (.out(CLK_out));
  Counter #(.max('h3ffff), .width(18)) counter_1 (
    .clk(CLK_out), .carry(counter_1_carry), .Q(CYCLE));  // open: clr, load, up, count, D
  not not_1 (not_1_out, ACK);
  Random #(.seed(100), .width(32)) random_1 (.clk(CLK_out), .out(random_1_out));  // open: clr, next
  Counter #(.max('he), .ongoal("stay"), .width(4)) counter_2 (
    .count(NXTOP), .clk(CLK_out), .carry(counter_2_carry), .Q(counter_2_q));  // open: clr, load, up, D
  Register #(.width(32)) register_1 (.D(random_1_out), .en(NXTOP), .clk(CLK_out), .Q(register_1_q));  // open: clr
  or or_1 (OLDNXTOP, EdgeACK, and_1_out);
  and and_1 (and_1_out, REdgeRST, GT2RST);
  and and_2 (and_2_out, REdgeRST, GT2RST);
  GenPulseAtNegEdge genpulseatnegedge_1 (.CLK(CLK_out), .X(ACK), .PULSE(FEdgeACK));
  GenPulseAtNegEdge genpulseatnegedge_2 (.CLK(CLK_out), .X(not_1_out), .PULSE(REdgeACK));
  Multiplexer #(.width(32)) multiplexer_1 (.in0(register_1_q), .in1(32'hffff7f7f), .out(DINb), .sel(1'b0));
  ROM #(.addrWidth(4), .dataWidth(32)) EdgeCases (.addr(counter_2_q), .data(EdgeCases_data));
  or or_2 (NXTOP, FEdgeREQ, and_2_out);
  SysRunnerL sysrunnerl_1 (
    .CLK(CLK_out), .RUNMIN(16'h2000), .RUNMAX(16'hfffe), .RSTMIN(13'h1), .RSTMAX(13'h8), .RST(RST));
  or or_3 (EdgeACK, FEdgeACK, REdgeACK);
  not not_2 (not_2_out, RST);
  not not_3 (not_3_out, REQ);
  CountNegEdges16b countnegedges16b_1 (
    .CLK(CLK_out), .X(RST), .REACHEDMAX(countnegedges16b_1_reachedmax), .COUNT(CNTRST));
  GenPulseAtNegEdge genpulseatnegedge_3 (.CLK(CLK_out), .X(not_2_out), .PULSE(REdgeRST));
  DUT dut_1 (.X1(X1), .Y1(Y1), .X2(X2), .Y2(Y2), .REQ(REQ), .CLK(CLK_out), .RST(RST), .DIST(DIST), .ACK(ACK));
  Random #(.seed(43), .width(32)) random_2 (.next(REdgeACK), .clk(CLK_out), .out(random_2_out));  // open: clr
  RndDlyHSClient rnddlyhsclient_1 (.CLK(CLK_out), .RST(RST), .ACK(ACK), .REQ(REQ));
  GenPulseAtNegEdge genpulseatnegedge_4 (.CLK(CLK_out), .X(REQ), .PULSE(FEdgeREQ));
  GenPulseAtNegEdge genpulseatnegedge_5 (.CLK(CLK_out), .X(not_3_out), .PULSE(REdgeREQ));
  Comparator #(.mode("unsigned"), .width(16)) comparator_1 (.a(CNTRST), .b({16{1'b0}}), .gt(GT2RST));  // open: eq, lt
  // Probe on multiplexer_2_out
  Multiplexer #(.width(32)) multiplexer_2 (
    .in0(EdgeCases_data), .in1(DINb), .out(multiplexer_2_out), .sel(counter_2_carry));
  LED led_1 (.in(RST));
  LED led_2 (.in(REQ));
  LED led_3 (.in(ACK));
  or or_4 (or_4_out, FEdgeREQ, REdgeREQ);
  Multiplexer #(.width(32)) multiplexer_3 (
    .in0(random_2_out), .in1(multiplexer_2_out), .out({Y2, X2, Y1, X1}), .sel(REQ));
  PulseCounter16b pulsecounter16b_1 (.CLK(CLK_out), .PULSE(or_4_out), .COUNT(CNTREQ));  // open: RST, REACHEDMAX
  PulseCounter16b pulsecounter16b_2 (
    .CLK(CLK_out), .PULSE(EdgeACK), .REACHEDMAX(pulsecounter16b_2_reachedmax), .COUNT(CNTACK));  // open: RST
  or or_5 (halt, counter_1_carry, countnegedges16b_1_reachedmax, pulsecounter16b_2_reachedmax);
  Subtractor #(.width(16)) subtractor_1 (.a(CNTREQ), .b(CNTACK), .out(subtractor_1_out));  // open: bin, bout
  Comparator #(.width(16)) comparator_2 (.a(subtractor_1_out), .b(16'h2), .lt(ASSERTIONS));  // open: gt, eq

  // Other names for the same wires on the sheet: DIN[31:0] = {Y2, X2, Y1, X1}

  // Notes on the sheet:
  //   contents of EdgeCases (hex, n*v repeats v):
  //   0 ffffffff fffff 7f7f 7fff7fff 7f7fffff ff7f7fff 7f7f0000 7fff0000 3f3f8080 3f3f00 808000 7f7f7f7f
  //   fedcba 456789 dcba98
  //   Edge@Ack
  //   Change to 1 to use constant DIN
  //   Edge@Req
endmodule

module CountNegEdges16b (
  input  CLK,
  input  X,
  output REACHEDMAX,
  output [15:0] COUNT
);

  wire genpulseatnegedge_1_pulse;

  GenPulseAtNegEdge genpulseatnegedge_1 (.CLK(CLK), .X(X), .PULSE(genpulseatnegedge_1_pulse));
  Counter #(.max('hffff), .width(16)) counter_1 (
    .count(genpulseatnegedge_1_pulse), .clk(CLK), .carry(REACHEDMAX), .Q(COUNT));  // open: clr, load, up, D
endmodule
